# Fritzing sketch Circuit (saved by Fritzing 0.9.3b)
breadboards: 1

parts:
  Load_Cell2 = Load Cell - Red/white/black/green
  Part2 = HX711 Weighing Sensor Module
  Load_Cell3 = Load Cell - Red/white/black/green
  Part3 = HX711 Weighing Sensor Module
  Mod1 = Heltec WiFi LoRa 32 V3 [part_number=HTIT-WB32LA]
  S1 = Pushbutton [package="[SMD]"]
  R1 = Resistor [tolerance=±5% resistance=10k package="0402 [SMD]"]
  J1 = Basic Servo
  J3 = Basic Servo
  Mod2 = KY-019 5V Relay Module [package="Breakout board"]
  WATER_PUMP1 = water pump/motor  # not connected

nets:
  N1: Load_Cell2.wire1, Part2.E+
  N2: Load_Cell2.wire2, Part2.A+
  N3: Load_Cell2.wire3, Part2.E-
  N4: Load_Cell2.wire4, Part2.A-
  VCC: Part2.VCC, Part3.VCC, Mod1.pin_20, S1.Pin_3, S1.Pin_4, J1.vcc, J3.vcc, Mod2.+
  GND: Part2.GND, Part3.GND, Mod1.pin_18, Mod1.pin_19, R1.Pin_1, J1.gnd, J3.gnd, Mod2.-
  N5: Part2.DO/RX, Mod1.pin_14
  N6: Part2.CK/TX, Mod1.pin_15
  N7: Load_Cell3.wire1, Part3.E+
  N8: Load_Cell3.wire2, Part3.A+
  N9: Load_Cell3.wire3, Part3.E-
  N10: Load_Cell3.wire4, Part3.A-
  N11: Part3.DO/RX, Mod1.pin_12
  N12: Part3.CK/TX, Mod1.pin_13
  N13: Mod1.pin_32, S1.Pin_1, S1.Pin_2, R1.Pin_0
  N14: Mod1.pin_34, Mod2.S

custom parts:
  Load Cell - Red/white/black/green: A rectangle load cell/weighting pressure Sensor with four wires - Red, white, black, green. Normally corresponding with E+, E-, A+, A- respectively.
  HX711 Weighing Sensor Module: HX711 is a precision 24-bit analog-to-digital converter (ADC) designed for weigh scales and industrial control applications to interface directly with a bridge sensor.
  Heltec WiFi LoRa 32 V3: The Heltec WiFi LoRa 32 is an IoT development board designed and produced by Heltec Automation and based on the Espressif ESP32-S3FN8 and Semtech SX1262 modules. The board includes WiFi, Bluetooth and LoRa functions, as well as a 0.96″ OLED display and a lithium battery management system. Links: Heltec WiFi LoRa 32 product page Github
  KY-019 5V Relay Module: KY-019 5V Relay module, used to control AC circuits. (Special thanks to vanepp for fixing the PCB holes and other errors)
  water pump/motor: WATER PUMP BY ARDUBLOCKTR
